// Logisim project Problem1.circ as structural Verilog: 2 circuits, main circuit F
module F (
  input  a,
  input  b,
  input  c,
  output F0
);

  wire and_1_out, and_2_out, or_1_out, or_2_out, or_3_out;

  and and_1 (and_1_out, a, b);
  or or_1 (or_1_out, a, b);
  and and_2 (and_2_out, and_1_out, c);
  or or_2 (or_2_out, c, or_1_out);
  or or_3 (or_3_out, and_2_out, and_1_out);
  or or_4 (F0, or_3_out, or_2_out);

  // Notes on the sheet:
  //   ab
  //   a+b
  //   abc
  //   a+b+c
  //   ab+abc
  //   abc+ab+a+b+c
endmodule

module G (
  input  a,
  input  b,
  input  c,
  output G0
);

  wire and_1_out, and_2_out, and_3_out, and_4_out, and_5_out, and_6_out, not_1_out, not_2_out, not_3_out,
       or_1_out;

  not not_1 (not_1_out, a);
  not not_2 (not_2_out, b);
  not not_3 (not_3_out, b);
  and and_1 (and_1_out, not_1_out, not_2_out);
  and and_2 (and_2_out, a, not_3_out);
  and and_3 (and_3_out, a, b);
  and and_4 (and_4_out, and_1_out, c);
  and and_5 (and_5_out, and_2_out, c);
  and and_6 (and_6_out, and_3_out, c);
  or or_1 (or_1_out, and_4_out, and_5_out);
  or or_2 (G0, or_1_out, and_6_out);

  // Notes on the sheet:
  //   ab
  //   a'b'
  //   a'b'c
  //   ab'
  //   ab'c
  //   abc
  //   a'b'c+ab'c
  //   abc+a'b'c+ab'c
endmodule
