// Logisim project Problem1.circ as structural Verilog: 3 circuits, main circuit main
module main (
  input  [7:0] addr,
  input  [2:0] ControlSignal
);

  wire clk_out, decode_1_o_0, decode_1_o_1, decode_1_o_2, decode_1_o_4, decode_1_o_5;
  wire [7:0] controlled_buffer_1_out, iocontroller_1_busout, RandomAccessMemory_dout, ReadOnlyMemory_data;

  Clock clk (.out(clk_out));
  ROM ReadOnlyMemory (.addr(addr), .data(ReadOnlyMemory_data));
  Decode decode_1 (
    .ControlSig(ControlSignal), .O_0(decode_1_o_0), .O_1(decode_1_o_1), .O_2(decode_1_o_2),
    .O_4(decode_1_o_4), .O_5(decode_1_o_5));
  RAM RandomAccessMemory (
    .addr(addr), .we(decode_1_o_1), .oe(decode_1_o_2), .clk(clk_out), .dout(RandomAccessMemory_dout));  // open: din
  assign RandomAccessMemory_dout = decode_1_o_0 ? ~ReadOnlyMemory_data : 8'bz;  // Controlled_Inverter controlled_inverter_1
  assign controlled_buffer_1_out = decode_1_o_4 ? RandomAccessMemory_dout : 8'bz;  // Controlled_Buffer controlled_buffer_1
  assign RandomAccessMemory_dout = decode_1_o_5 ? iocontroller_1_busout : 8'bz;  // Controlled_Buffer controlled_buffer_2
  IOController iocontroller_1 (
    .addr(addr), .BusIN(controlled_buffer_1_out), .CtrlSig(ControlSignal), .BusOUT(iocontroller_1_busout));  // open: I_Dev0, I_Dev1, I_Dev2, I_Dev3, O_Dev0, O_Dev1, O_Dev2, O_Dev3
endmodule

module IOController (
  input  [7:0] I_Dev0,
  input  [7:0] I_Dev1,
  input  [7:0] I_Dev2,
  input  [7:0] I_Dev3,
  input  [7:0] addr,
  input  [7:0] BusIN,
  input  [2:0] CtrlSig,
  output [7:0] O_Dev0,
  output [7:0] O_Dev1,
  output [7:0] O_Dev2,
  output [7:0] O_Dev3,
  output [7:0] BusOUT
);

  wire and_1_out, and_2_out, not_1_out, not_2_out, not_3_out;
  wire [7:0] controlled_buffer_2_out, multiplexer_1_out;

  Multiplexer #(.select(2), .width(8)) multiplexer_1 (
    .in0(I_Dev0), .in1(I_Dev1), .in2(I_Dev2), .in3(I_Dev3), .out(multiplexer_1_out), .sel(addr[7:6]));
  not not_1 (not_1_out, CtrlSig[0]);
  not not_2 (not_2_out, CtrlSig[1]);
  not not_3 (not_3_out, CtrlSig[2]);
  assign BusOUT = and_1_out ? multiplexer_1_out : 8'bz;  // Controlled_Buffer controlled_buffer_1
  assign controlled_buffer_2_out = and_2_out ? BusIN : 8'bz;  // Controlled_Buffer controlled_buffer_2
  and and_1 (and_1_out, not_1_out, not_2_out, CtrlSig[2]);
  and and_2 (and_2_out, CtrlSig[0], CtrlSig[1], not_3_out);
  Demultiplexer #(.select(2), .width(8)) demultiplexer_1 (
    .out0(O_Dev0), .out1(O_Dev1), .out2(O_Dev2), .out3(O_Dev3), .in(controlled_buffer_2_out), .sel(addr[7:6]));
endmodule

module Decode (
  input  [2:0] ControlSig,
  output O_0,
  output O_1,
  output O_2,
  output O_4,
  output O_5
);

  wire not_1_out, not_2_out, not_3_out;

  not not_1 (not_1_out, ControlSig[2]);
  not not_2 (not_2_out, ControlSig[1]);
  not not_3 (not_3_out, ControlSig[0]);
  and and_1 (O_0, not_1_out, not_2_out, not_3_out);
  and and_2 (O_1, not_1_out, not_2_out, ControlSig[0]);
  and and_3 (O_2, not_1_out, ControlSig[1], not_3_out);
  and and_4 (O_4, not_1_out, ControlSig[1], ControlSig[0]);
  and and_5 (O_5, ControlSig[2], not_2_out, not_3_out);
endmodule
