// Logisim project Problem2.circ as structural Verilog
module main (
  input  [7:0] in_1,
  input  [7:0] in_2,
  input  in_3,
  input  [7:0] in_4,
  input  [7:0] in_5,
  input  in_6,
  input  [7:0] in_7,
  input  [7:0] in_8,
  input  in_9,
  input  [7:0] in_10,
  input  [7:0] in_11,
  input  [7:0] in_12,
  input  [7:0] in_13,
  input  [7:0] in_14,
  input  [7:0] in_15,
  output out_16,
  output [7:0] out_17,
  output out_18,
  output [7:0] out_19,
  output out_20,
  output [7:0] out_21,
  output [7:0] out_22,
  output [7:0] out_23,
  output [7:0] out_24
);

  EightBitAdder eightbitadder_1 (.A(in_1), .B(in_2), .Ci(in_3), .Co(out_16), .S(out_17));
  EightBitAdder eightbitadder_2 (.A(in_4), .B(in_5), .Ci(in_6), .Co(out_18), .S(out_19));
  EightBitAdder eightbitadder_3 (.A(in_7), .B(in_8), .Ci(in_9), .Co(out_20), .S(out_21));
  EightBitSubtractor eightbitsubtractor_1 (.in_1(in_10), .in_2(in_11), .out_3(out_22));
  EightBitSubtractor eightbitsubtractor_2 (.in_1(in_12), .in_2(in_13), .out_3(out_23));
  EightBitSubtractor eightbitsubtractor_3 (.in_1(in_14), .in_2(in_15), .out_3(out_24));
endmodule

module SingleBitAdder (
  input  A,
  input  B,
  input  Ci,
  output Co,
  output S
);

  wire and_1_out, and_2_out, and_3_out;

  and and_1 (and_1_out, A, B);
  and and_2 (and_2_out, A, Ci);
  and and_3 (and_3_out, B, Ci);
  or or_1 (Co, and_1_out, and_2_out, and_3_out);
  xor xor_1 (S, A, B, Ci);
endmodule

module EightBitAdder (
  input  [7:0] A,
  input  [7:0] B,
  input  Ci,
  output Co,
  output [7:0] S
);

  wire singlebitadder_1_co, singlebitadder_2_co, singlebitadder_3_co, singlebitadder_4_co,
       singlebitadder_5_co, singlebitadder_6_co, singlebitadder_7_co;

  SingleBitAdder singlebitadder_1 (.A(A[0]), .B(B[0]), .Ci(Ci), .Co(singlebitadder_1_co), .S(S[0]));
  SingleBitAdder singlebitadder_2 (.A(A[1]), .B(B[1]), .Ci(singlebitadder_1_co), .Co(singlebitadder_2_co), .S(S[1]));
  SingleBitAdder singlebitadder_3 (.A(A[2]), .B(B[2]), .Ci(singlebitadder_2_co), .Co(singlebitadder_3_co), .S(S[2]));
  SingleBitAdder singlebitadder_4 (.A(A[3]), .B(B[3]), .Ci(singlebitadder_3_co), .Co(singlebitadder_4_co), .S(S[3]));
  SingleBitAdder singlebitadder_5 (.A(A[4]), .B(B[4]), .Ci(singlebitadder_4_co), .Co(singlebitadder_5_co), .S(S[4]));
  SingleBitAdder singlebitadder_6 (.A(A[5]), .B(B[5]), .Ci(singlebitadder_5_co), .Co(singlebitadder_6_co), .S(S[5]));
  SingleBitAdder singlebitadder_7 (.A(A[6]), .B(B[6]), .Ci(singlebitadder_6_co), .Co(singlebitadder_7_co), .S(S[6]));
  SingleBitAdder singlebitadder_8 (.A(A[7]), .B(B[7]), .Ci(singlebitadder_7_co), .Co(Co), .S(S[7]));
endmodule

module EightBitSubtractor (
  input  [7:0] in_1,
  input  [7:0] in_2,
  output [7:0] out_3
);

  wire eightbitadder_1_co;
  wire [7:0] not_1_out;

  assign not_1_out = ~in_2;  // NOT_Gate not_1, 8 bits wide
  EightBitAdder eightbitadder_1 (.A(in_1), .B(not_1_out), .Ci(1'b1), .Co(eightbitadder_1_co), .S(out_3));
endmodule

module L1 (
  input  [7:0] A,
  input  Shift,
  output [7:0] O
);

  Multiplexer multiplexer_1 (.in0(A[7]), .in1(A[6]), .out(O[7]), .sel(Shift));
  Multiplexer multiplexer_2 (.in0(A[6]), .in1(A[5]), .out(O[6]), .sel(Shift));
  Multiplexer multiplexer_3 (.in0(A[5]), .in1(A[4]), .out(O[5]), .sel(Shift));
  Multiplexer multiplexer_4 (.in0(A[4]), .in1(A[3]), .out(O[4]), .sel(Shift));
  Multiplexer multiplexer_5 (.in0(A[3]), .in1(A[2]), .out(O[3]), .sel(Shift));
  Multiplexer multiplexer_6 (.in0(A[2]), .in1(A[1]), .out(O[2]), .sel(Shift));
  Multiplexer multiplexer_7 (.in0(A[1]), .in1(A[0]), .out(O[1]), .sel(Shift));
  Multiplexer multiplexer_8 (.in0(A[0]), .in1(1'b0), .out(O[0]), .sel(Shift));
endmodule
